# Fritzing sketch ArduinoOneWireDHT12 (saved by Fritzing 0.9.3b)
breadboards: 1

parts:
  Componente1 = Arduino Uno (Rev3)
  RHT1 = Humidity and Temperature Sensor RHT03
  R1 = Resistor [tolerance=±5% resistance=4.7 package=THT]

nets:
  N1: Componente1.D5_PWM, RHT1.Data-signal, R1.Pin_1
  5V: Componente1.5V, RHT1.Vcc, R1.Pin_0
  N2: Componente1.GND, RHT1.GND_1, RHT1.GND_2

notes:
  4.7K
