# Fritzing sketch ArduinoI2CDHT12 (saved by Fritzing 0.9.3b)
breadboards: 1

parts:
  Componente1 = Arduino Uno (Rev3)
  R1 = Resistor [tolerance=±5% resistance=4.7k package=THT]
  R2 = Resistor [tolerance=±5% resistance=4.7k package=THT]
  RHT1 = Humidity and Temperature Sensor RHT03

nets:
  N1: Componente1.A4/SDA, R2.Pin_1, RHT1.Data-signal
  N2: Componente1.A5/SCL, R1.Pin_0, RHT1.GND_2
  5V: Componente1.5V, R1.Pin_1, R2.Pin_0, RHT1.Vcc
  N3: Componente1.GND, RHT1.GND_1

notes:
  4.7K
